# Fritzing sketch schema (saved by Fritzing 0.9.3b)
breadboards: 1

parts:
  Composant1 = Arduino Uno (Rev3)
  ZS-042_RTC1 = ZS-042 RTC Module
  LED2 = LED - 5mm [color="Red (633nm)" package="5 mm [THT]"]
  LED3 = LED - 5mm [color="Green (555nm)" package="5 mm [THT]"]
  LED4 = LED - 5mm [color="Orange (620nm)" package="5 mm [THT]"]
  R6 = Resistor [tolerance=±5% resistance=10k package=THT]
  R7 = Resistor [tolerance=±5% resistance=10k package=THT]
  R8 = Resistor [tolerance=±5% resistance=10k package=THT]

nets:
  N1: Composant1.A4/SDA, ZS-042_RTC1.SDA
  N2: Composant1.A5/SCL, ZS-042_RTC1.SCL
  N3: Composant1.D3_PWM, R8.Pin_0
  N4: Composant1.D5_PWM, R7.Pin_0
  N5: Composant1.D6_PWM, R6.Pin_0
  5V: Composant1.5V, ZS-042_RTC1.VCC
  GND: Composant1.GND, ZS-042_RTC1.GND, LED2.cathode, LED3.cathode, LED4.cathode
  N6: LED2.anode, R6.Pin_1
  N7: LED3.anode, R8.Pin_1
  N8: LED4.anode, R7.Pin_1
