# Fritzing sketch push_button_led (saved by Fritzing 0.9.3b)
breadboards: 1

parts:
  Raspberry_Pi_B_rev1 = Raspberry Pi B rev1
  S1 = Pushbutton [package="[SMD]"]
  LED1 = smd LED [color="Red (633nm)" package="0805 [SMD]"]
  R2 = Resistor [tolerance=±5% resistance=220 package="2010 [SMD]"]

nets:
  N1: Raspberry_Pi_B_rev1.3V3, S1.Pin_3, S1.Pin_4
  N2: Raspberry_Pi_B_rev1.GND, R2.Pin_1
  N3: Raspberry_Pi_B_rev1.GPIO_17, LED1.anode
  N4: Raspberry_Pi_B_rev1.GPIO_22, S1.Pin_1, S1.Pin_2
  N5: LED1.cathode, R2.Pin_0
